# Fritzing sketch Potentiometer LED Schematic (saved by Fritzing 0.9.2b)
circuit board: 8.46667cm x 5.64444cm
breadboards: 1

parts:
  Part1 = Arduino Uno (Rev3) - ICSP
  R1 = Resistor [tolerance=±5% resistance=330 package="0603 [SMD]"]
  POT1 = Breadboard Trimpot
  LED1 = smd LED [color="Red (633nm)" package="0603 [SMD]"]

nets:
  N1: Part1.A0, POT1.PIN2
  N2: Part1.5V, R1.Pin_0, R1.Pin_1, POT1.PIN3, LED1.cathode
  N3: Part1.GND, POT1.PIN1
  N4: Part1.D13/SCK, LED1.anode

// code stored in the sketch: Blink_LED_Schematic.ino
/*
This was also rewritten/explained from the Sparkfun Inventor's Kit with my work included.

Hardware explanation:
We're going to be using a potentiomter, which is an analog signal
instead of a digital signal.

Since it is analog, it doesn't output either 0V for low or 5V for high,
but it actually can output a range from 0V - 5V.

We're going to use the potentiometer to control the speed
an LED blinks on the circuit.
*/

//Let's define our fields.
int sensorPin = 0;    // The potentiometer is connected to analog pin 0
                      
int ledPin = 13;      // The LED is connected to digital pin 13

//Let's make our setup method.
void setup(
{
  pinMode(ledPin, OUTPUT); // We declared ledPin is pin 13.
                         				  // We can use it as a variable here.

  // Sensor pin not needed to be mentioned because it's an
  // analog signal. Analog signals are already input signals,
  // therefore, there is no need to mention them at setup.
}

//Make our loop() method.
void loop()
{
  // Create a variable inside this method to store the voltage of pot.
  // analogRead() is a method in Arduino library that reads the analog
  // signal and then converts it to a number.
  // 0(0V) - 1023(5V).
  int sensorValue = analogRead(sensorPin); //sensorPin = pin 13 

  //Use the sensorValue to be the delay.
  digitalWrite(ledPin, HIGH);     // Turn the LED on
  delay(sensorValue);             // Pause for x milliseconds.
  
  digitalWrite(ledPin, LOW);      // Turn the LED off
  delay(sensorValue);             // Pause for x milliseconds.
}

// code stored in the sketch: Potentiometer_LED.ino
/*
This was also rewritten/explained from the Sparkfun Inventor's Kit with my work included.

Hardware explanation:
We're going to be using a potentiomter, which is an analog signal
instead of a digital signal.

Since it is analog, it doesn't output either 0V for low or 5V for high,
but it actually can output a range from 0V - 5V.

We're going to use the potentiometer to control the speed
an LED blinks on the circuit.
*/

//Let's define our fields.
int sensorPin = 0;    // The potentiometer is connected to analog pin 0
                      
int ledPin = 13;      // The LED is connected to digital pin 13

//Let's make our setup method.
void setup(
{
  pinMode(ledPin, OUTPUT); // We declared ledPin is pin 13.
                           // We can use it as a variable here.
                           
  // Sensor pin not needed to be mentioned because it's an
  // analog signal. Analog signals are already input signals,
  // therefore, there is no need to mention them at setup.
}

//Make our loop() method.
void loop()
{
  // Create a variable inside this method to store the voltage of pot.
  // analogRead() is a method in Arduino library that reads the analog
  // signal and then converts it to a number.
  // 0(0V) - 1023(5V).
  int sensorValue = analogRead(sensorPin); //sensorPin = pin 13 

  //Use the sensorValue to be the delay.
  digitalWrite(ledPin, HIGH);     // Turn the LED on
  delay(sensorValue);             // Pause for x milliseconds.
  
  digitalWrite(ledPin, LOW);      // Turn the LED off
  delay(sensorValue);             // Pause for x milliseconds.
}
