# Fritzing sketch RGB LED Schematic (saved by Fritzing 0.9.2b)
circuit board: 8.46667cm x 5.64444cm
breadboards: 1

parts:
  Arduino = Arduino Uno (Rev3) - ICSP
  LED1 = RGB LED (com. cathode, rgb) [package="5 mm [THT]"]
  R1 = Resistor [tolerance=±5% resistance=330 package="0402 [SMD]"]
  R2 = Resistor [tolerance=±5% resistance=330 package="0402 [SMD]"]
  R3 = Resistor [tolerance=±5% resistance=330 package="0402 [SMD]"]

nets (from the breadboard view):
  N1: Arduino.GND, LED1.common_cathode
  N2: Arduino.D9_PWM, R1.Pin_0
  N3: Arduino.D10_PWM/SS, R2.Pin_0
  N4: Arduino.D11_PWM/MOSI, R3.Pin_0
  N5: LED1.red_anode, R1.Pin_1
  N6: LED1.green_anode, R2.Pin_1
  N7: LED1.blue_anode, R3.Pin_1

// code stored in the sketch: Blink_LED_Schematic.ino
/*
This was also rewritten/explained from the Sparkfun Inventor's Kit with my work included.

Hardware connections:
  The RGB light actually has 3 LEDS inside that merge to make new colors.
  Therefore, we need 3 resistors, one for each LED inside the RGB LED.  
*/

//Define fields here.
//const is used to set the variable to static so it cannot be changed.
//const is not required in this example but is good form.
const int RED_PIN = 9;
const int GREEN_PIN = 10;
const int BLUE_PIN = 11;

//Variable to display each LED
int DISPLAY_TIME = 100;  // In milliseconds


void setup()
{
  
  pinMode(RED_PIN, OUTPUT);
  pinMode(GREEN_PIN, OUTPUT);
  pinMode(BLUE_PIN, OUTPUT);
}


void loop()
{
  //Create a method that goes through all the colors.
  mainColors();

  //Create a method that smoothly transitions all the colors.
  showSpectrum();
}

//This method goes through every combination 
void mainColors()
{
  // Off (all LEDs off):
  digitalWrite(RED_PIN, LOW);
  digitalWrite(GREEN_PIN, LOW);
  digitalWrite(BLUE_PIN, LOW);
  
  delay(1000); //delay all this 

  // Red (turn just the red LED on):
  digitalWrite(RED_PIN, HIGH);
  digitalWrite(GREEN_PIN, LOW);
  digitalWrite(BLUE_PIN, LOW);
  
  delay(1000);

  // Green (turn just the green LED on):
  digitalWrite(RED_PIN, LOW);
  digitalWrite(GREEN_PIN, HIGH);
  digitalWrite(BLUE_PIN, LOW);
  
  delay(1000);

  // Blue (turn just the blue LED on):
  digitalWrite(RED_PIN, LOW);
  digitalWrite(GREEN_PIN, LOW);
  digitalWrite(BLUE_PIN, HIGH);
  
  delay(1000);

  // Yellow (turn red and green on):

  digitalWrite(RED_PIN, HIGH);
  digitalWrite(GREEN_PIN, HIGH);
  digitalWrite(BLUE_PIN, LOW);

  delay(1000);

  // Cyan (turn green and blue on):

  digitalWrite(RED_PIN, LOW);
  digitalWrite(GREEN_PIN, HIGH);
  digitalWrite(BLUE_PIN, HIGH);

  delay(1000);

  // Purple (turn red and blue on):

  digitalWrite(RED_PIN, HIGH);
  digitalWrite(GREEN_PIN, LOW);
  digitalWrite(BLUE_PIN, HIGH);

  delay(1000);

  // White (turn all the LEDs on):

  digitalWrite(RED_PIN, HIGH);
  digitalWrite(GREEN_PIN, HIGH);
  digitalWrite(BLUE_PIN, HIGH);

  delay(1000);
}

//This method transitions through the colors smoothly.
void showSpectrum()
{
  for (int x = 0; x < 768; x++)
  {
    showRGB(x);  // Call RGBspectrum() with our new x
    delay(10);   // Delay for 10 ms (1/100th of a second)
  }
}

// This method goes through each number in the for loop from 0 to 767.
// Each number determines the intensity of the current color so it goes
// through each shade of color in the spectrum.

// Since intensity base colors start and end at red, so the loop will
// make the colors seem continuously looping. Numbers between or above
// the listed numbers will create blends in the colors. 

// The "base" numbers are:
// 0   = pure red
// 255 = pure green
// 511 = pure blue
// 767 = pure red (again)

void showRGB(int color)
{
  int redIntensity;
  int greenIntensity;
  int blueIntensity;

  if (color <= 255)
  {
    redIntensity = 255 - color;    // red goes from on to off
    greenIntensity = color;        // green goes from off to on
    blueIntensity = 0;             // blue is always off
  }
  else if (color <= 511)
  {
    redIntensity = 0;                     // red is always off
    greenIntensity = 255 - (color - 256); // green on to off
    blueIntensity = (color - 256);        // blue off to on
  }
  else // color >= 512
  {
    redIntensity = (color - 512);         // red off to on
    greenIntensity = 0;                   // green is always off
    blueIntensity = 255 - (color - 512);  // blue on to off
  }

  // Write value to LEDs.
  analogWrite(RED_PIN, redIntensity);
  analogWrite(BLUE_PIN, blueIntensity);
  analogWrite(GREEN_PIN, greenIntensity);
}

// code stored in the sketch: RGB_LED.ino
/*
This was also rewritten/explained from the Sparkfun Inventor's Kit with my work included.

Hardware connections:
  The RGB light actually has 3 LEDS inside that merge to make new colors.
  Therefore, we need 3 resistors, one for each LED inside the RGB LED.  
*/

//Define fields here.
//const is used to set the variable to static so it cannot be changed.
//const is not required in this example but is good form.
const int RED_PIN = 9;
const int GREEN_PIN = 10;
const int BLUE_PIN = 11;

//Variable to display each LED
int DISPLAY_TIME = 100;  // In milliseconds


void setup()
{
  
  pinMode(RED_PIN, OUTPUT);
  pinMode(GREEN_PIN, OUTPUT);
  pinMode(BLUE_PIN, OUTPUT);
}


void loop()
{
  //Create a method that goes through all the colors.
  mainColors();

  //Create a method that smoothly transitions all the colors.
  showSpectrum();
}

//This method goes through every combination 
void mainColors()
{
  // Off (all LEDs off):
  digitalWrite(RED_PIN, LOW);
  digitalWrite(GREEN_PIN, LOW);
  digitalWrite(BLUE_PIN, LOW);
  
  delay(1000); //delay all this 

  // Red (turn just the red LED on):
  digitalWrite(RED_PIN, HIGH);
  digitalWrite(GREEN_PIN, LOW);
  digitalWrite(BLUE_PIN, LOW);
  
  delay(1000);

  // Green (turn just the green LED on):
  digitalWrite(RED_PIN, LOW);
  digitalWrite(GREEN_PIN, HIGH);
  digitalWrite(BLUE_PIN, LOW);
  
  delay(1000);

  // Blue (turn just the blue LED on):
  digitalWrite(RED_PIN, LOW);
  digitalWrite(GREEN_PIN, LOW);
  digitalWrite(BLUE_PIN, HIGH);
  
  delay(1000);

  // Yellow (turn red and green on):

  digitalWrite(RED_PIN, HIGH);
  digitalWrite(GREEN_PIN, HIGH);
  digitalWrite(BLUE_PIN, LOW);

  delay(1000);

  // Cyan (turn green and blue on):

  digitalWrite(RED_PIN, LOW);
  digitalWrite(GREEN_PIN, HIGH);
  digitalWrite(BLUE_PIN, HIGH);

  delay(1000);

  // Purple (turn red and blue on):

  digitalWrite(RED_PIN, HIGH);
  digitalWrite(GREEN_PIN, LOW);
  digitalWrite(BLUE_PIN, HIGH);

  delay(1000);

  // White (turn all the LEDs on):

  digitalWrite(RED_PIN, HIGH);
  digitalWrite(GREEN_PIN, HIGH);
  digitalWrite(BLUE_PIN, HIGH);

  delay(1000);
}

//This method transitions through the colors smoothly.
void showSpectrum()
{
  for (int x = 0; x < 768; x++)
  {
    showRGB(x);  // Call RGBspectrum() with our new x
    delay(10);   // Delay for 10 ms (1/100th of a second)
  }
}

// This method goes through each number in the for loop from 0 to 767.
// Each number determines the intensity of the current color so it goes
// through each shade of color in the spectrum.

// Since intensity base colors start and end at red, so the loop will
// make the colors seem continuously looping. Numbers between or above
// the listed numbers will create blends in the colors. 

// The "base" numbers are:
// 0   = pure red
// 255 = pure green
// 511 = pure blue
// 767 = pure red (again)

void showRGB(int color)
{
  int redIntensity;
  int greenIntensity;
  int blueIntensity;

  if (color <= 255)
  {
    redIntensity = 255 - color;    // red goes from on to off
    greenIntensity = color;        // green goes from off to on
    blueIntensity = 0;             // blue is always off
  }
  else if (color <= 511)
  {
    redIntensity = 0;                     // red is always off
    greenIntensity = 255 - (color - 256); // green on to off
    blueIntensity = (color - 256);        // blue off to on
  }
  else // color >= 512
  {
    redIntensity = (color - 512);         // red off to on
    greenIntensity = 0;                   // green is always off
    blueIntensity = 255 - (color - 512);  // blue on to off
  }

  // Write value to LEDs.
  analogWrite(RED_PIN, redIntensity);
  analogWrite(BLUE_PIN, blueIntensity);
  analogWrite(GREEN_PIN, greenIntensity);
}
