# Fritzing sketch Blink Multiple LEDs Schematic (saved by Fritzing 0.9.2b)
circuit board: 9.80962cm x 5.7749cm
breadboards: 1

parts:
  LED1 = LED - 3mm [color="Yellow (595nm)" package="3 mm [THT]"]
  LED3 = LED - 3mm [color="Yellow (595nm)" package="3 mm [THT]"]
  LED4 = LED - 3mm [color="Yellow (595nm)" package="3 mm [THT]"]
  LED5 = LED - 3mm [color="Yellow (595nm)" package="3 mm [THT]"]
  LED6 = LED - 3mm [color="Red (635nm)" package="3 mm [THT]"]
  LED7 = LED - 3mm [color="Red (635nm)" package="3 mm [THT]"]
  LED8 = LED - 3mm [color="Red (635nm)" package="3 mm [THT]"]
  LED9 = LED - 3mm [color="Red (635nm)" package="3 mm [THT]"]
  R1 = Resistor [tolerance=±5% resistance=330 package=THT]
  R2 = Resistor [tolerance=±5% resistance=330 package=THT]
  R3 = Resistor [tolerance=±5% resistance=330 package=THT]
  R4 = Resistor [tolerance=±5% resistance=330 package=THT]
  R5 = Resistor [tolerance=±5% resistance=330 package=THT]
  R6 = Resistor [tolerance=±5% resistance=330 package=THT]
  R7 = Resistor [tolerance=±5% resistance=330 package=THT]
  R8 = Resistor [tolerance=±5% resistance=330 package=THT]
  Part1 = Arduino Uno (Rev3)

nets:
  N1: LED1.cathode, R1.Pin_0
  N2: LED1.anode, Part1.D8
  N3: LED3.cathode, R2.Pin_0
  N4: LED3.anode, Part1.D7
  N5: LED4.cathode, R3.Pin_0
  N6: LED4.anode, Part1.D6_PWM
  N7: LED5.cathode, R4.Pin_0
  N8: LED5.anode, Part1.D5_PWM
  N9: LED6.cathode, R5.Pin_0
  N10: LED6.anode, Part1.D4
  N11: LED7.cathode, R6.Pin_0
  N12: LED7.anode, Part1.D3_PWM
  N13: LED8.cathode, R7.Pin_0
  N14: LED8.anode, Part1.D10_PWM/SS
  N15: LED9.cathode, R8.Pin_0
  N16: LED9.anode, Part1.D9_PWM
  N17: R1.Pin_1, R2.Pin_1, R3.Pin_1, R4.Pin_1, R5.Pin_1, R6.Pin_1, R7.Pin_1, R8.Pin_1, Part1.GND

// code stored in the sketch: Blink_Multiple_LEDs.ino.ino
/* Rewritten from Sparkfun Inventor's Kit.
Hardware connections:
  We are going to make 8 LEDs blink on and off in certain patterns.
*/

//Define fields
int ledPins[] = {2,3,4,5,6,7,8,9};
//In this array, we have 8 LEDs, and we indicate which pin they are referring to in order.


void setup()
{
  //Make a for loop to turn on all pins.
  for(int index = 0; index <= 7; index++)
  {
    pinMode(ledPins[index],OUTPUT);
  }
}

//Loop through any methods that you have indicated below.
void loop()
{
  //You can call any method (pattern) you want from the methods below and uncomment them for use.
  
  oneAfterAnotherLoop();    // Turn on each LED, one at a time.
    
  //oneOnAtATime();         // Turn on/off one LED at a time.

  //pingPong();             // Light the LEDs middle to the edges

  //marquee();              // Chase lights like you see on signs

  //randomLED();            // Blink LEDs randomly
}

//This method will light on each LED & then turn off each LED one at a time.
void oneAfterAnotherLoop()
{
  int delayTime = 100; // milliseconds to pause between LEDs
                       // make this smaller for faster switching

   // Loop & turn on all LEDs.
  for(int index = 0; index <= 7; index++)
  {
    digitalWrite(ledPins[index], HIGH);
    delay(delayTime);                
  }                                  

   // Loop & turn off all LEDs.
  for(int index = 7; index >= 0; index--)
  {
    digitalWrite(ledPins[index], LOW);
    delay(delayTime);
  }               
}

// This method will light on an LED and turn it off for each LED.
void oneOnAtATime()
{
  int delayTime = 100; // milliseconds to pause between LEDs

  // Loop through each LED. Turn it on and then off.
  for(int index = 0; index <= 7; index++)
  {
    digitalWrite(ledPins[index], HIGH);  // turn LED on
    delay(delayTime);                    // pause to slow down
    digitalWrite(ledPins[index], LOW);   // turn LED off
  }
}

// Go through the array to the end LED and then back, creating a ping-poing effect.
void pingPong()
{
  int delayTime = 100; // milliseconds to pause between LEDs

  //Go through each LED forwards with a loop.
  for(int index = 0; index <= 7; index++)
  {
    digitalWrite(ledPins[index], HIGH);  // turn LED on
    delay(delayTime);                    // pause to slow down
    digitalWrite(ledPins[index], LOW);   // turn LED off
  }

  // Go through each LED backwards with a loop.
  for(int index = 7; index >= 0; index--)
  {
    digitalWrite(ledPins[index], HIGH);  // turn LED on
    delay(delayTime);                    // pause to slow down
    digitalWrite(ledPins[index], LOW);   // turn LED off
  }
}


// Mimics "chase lights" like the signs.
void marquee()
{
  int delayTime = 200; // milliseconds to pause between LEDs

  // Loop through the first 4 LEDs, and then skip 4 and light up that one to make it seem like
  // it's chasing lights.
  for(int index = 0; index <= 3; index++) // Step from 0 to 3
  {
    digitalWrite(ledPins[index], HIGH);    // Turn a LED on
    digitalWrite(ledPins[index+4], HIGH);  // Skip four, and turn that LED on
    delay(delayTime);                      // Pause to slow down the sequence
    digitalWrite(ledPins[index], LOW);     // Turn the LED off
    digitalWrite(ledPins[index+4], LOW);   // Skip four, and turn that LED off
  }
}

// Lights up a random LED everytime.
void randomLED()
{
  int index = random(8);  // pick a random number between 0 and 7
  int delayTime = 100;
	
  digitalWrite(ledPins[index], HIGH);  // turn LED on
  delay(delayTime);                    // pause to slow down
  digitalWrite(ledPins[index], LOW);   // turn LED off
}
