# Fritzing sketch Basic Push Buttons Schematic (saved by Fritzing 0.9.2b)
circuit board: 8.46667cm x 5.64444cm
breadboards: 1

parts:
  Part2 = Arduino Uno (Rev3) - ICSP
  S1 = Pushbutton [package="[THT]"]
  S2 = Pushbutton [package="[THT]"]
  R1 = Resistor [tolerance=±5% resistance=220 package="2010 [SMD]"]
  R2 = Resistor [tolerance=±5% resistance=220 package="2010 [SMD]"]
  LED1 = LED - 3mm [color="Red (633nm)" package="3 mm [THT]"]
  R3 = Resistor [tolerance=±5% resistance=220 package="2010 [SMD]"]

nets:
  N1: Part2.5V, S1.Pin_3, S1.Pin_4, R1.Pin_1, R2.Pin_1, R3.Pin_0
  N2: Part2.GND, S2.Pin_3, S2.Pin_4
  N3: Part2.D13/SCK, LED1.anode
  N4: Part2.D2, S2.Pin_1, S2.Pin_2, R1.Pin_0
  N5: Part2.D3_PWM, S1.Pin_1, S1.Pin_2, R2.Pin_0
  N6: LED1.cathode, R3.Pin_1
